# Fritzing sketch waage_verdrahtung (saved by Fritzing 1.0.4)

parts:
  Rahmen1 = Bettrahmen  # not connected
  C3 = ESP32-C3 SuperMini
  HX711 = HX711 Weighing Sensor Module
  Zelle_1 = Waegezelle 50 kg (3 Draehte)
  Zelle_2 = Waegezelle 50 kg (3 Draehte)
  Zelle_3 = Waegezelle 50 kg (3 Draehte)
  Zelle_4 = Waegezelle 50 kg (3 Draehte)

nets:
  GND: C3.GND, HX711.GND
  3V3: C3.3V3, HX711.VCC
  N1: C3.GPIO4, HX711.CK/TX
  N2: C3.GPIO3, HX711.DO/RX
  N3: HX711.E+, Zelle_4.R
  N4: HX711.E-, Zelle_2.R
  N5: HX711.A+, Zelle_1.R
  N6: HX711.A-, Zelle_3.R
  N7: Zelle_1.W, Zelle_4.W
  N8: Zelle_1.B, Zelle_2.B
  N9: Zelle_2.W, Zelle_3.W
  N10: Zelle_3.B, Zelle_4.B

notes:
  Waage: ESP32-C3 SuperMini + HX711, Standard-Pins DT=GPIO3, SCK=GPIO4
  Waegezellen (am Aufbau getestet): R4=E+, R2=E-, R3=A+, R1=A-. W1-W4, W2-W3, B1-B2, B3-B4 verbinden. R=rot, W=weiss, B=schwarz. Das Herstellerschema (R1=E-, R2=A-) war nicht abgeglichen.
  HX711 um 180 Grad gedreht: VCC/SCK/DT liegen gegenueber 3V3/GPIO4/GPIO3, GND als laengere Leitung.

custom parts:
  Bettrahmen: Dekoration
  ESP32-C3 SuperMini: ESP32-C3 SuperMini (Waage)
  Waegezelle 50 kg (3 Draehte): Halbbruecken-Waegezelle, rot/weiss/schwarz
